# Fritzing sketch nerf-digital-target (saved by Fritzing 0.9.3b)
breadboards: 1

parts:
  Part1 = Adafruit Trinket 5V
  Part2 = 0.56" 7-segment LED Backpack [part_number=880]
  R1 = Resistor [tolerance=±5% resistance=100 package=THT]
  CLIP1 = Alligator Clip
  CLIP2 = Alligator Clip

nets:
  N1: Part1.#2, Part2.SCL
  N2: Part1.#0, Part2.SDA
  N3: Part1.#4, R1.Pin_0, CLIP2.wire
  +5V: Part1.+5V, Part2.VDD, CLIP1.wire

custom parts:
  Adafruit Trinket 5V: Trinket may be small, but do not be fooled by its size! It's a tiny microcontroller board, built around the Atmel ATtiny85, a little chip with a lot of power. We wanted to design a microcontroller board that was small enough to fit into any project, and low cost enough to use without hesitation. Perfect for when you don't want to give up your expensive dev-board and you aren't willing to take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
  0.56" 7-segment LED Backpack: This 0.56" 7-segment LED display includes a driver chip for simple control via an I2C interface. The backpack features address-selection jumpers so you can connect up to eight displays on a single I2C bus.
  Alligator Clip: Alligator clip
  Alligator Clip: Alligator clip
